# Fritzing sketch BreadboardVer (saved by Fritzing 0.9.3b)
breadboards: 1

parts:
  J1 = STM32 Nucleo boards
  C2 = Ceramic Capacitor [capacitance=100nF package="100 mil [THT, multilayer]"]
  TRRS1 = Audio Jack (TRRS) 3.5mm [part_number="LUMBERG JEITA RC-5325A" package="RC-5325A [SMD]"]
  Q2 = PNP-Transistor [package="TO92 [THT]"]
  R1 = Resistor [tolerance=±5% resistance=10k package=THT]
  R2 = Resistor [tolerance=±5% resistance=1.5k package=THT]
  R3 = Resistor [tolerance=±5% resistance=220 package=THT]
  C3 = Ceramic Capacitor [capacitance=100nF package="100 mil [THT, multilayer]"]

nets:
  N1: J1.D2, R1.Pin_0
  N2: J1.D6_PWM, R2.Pin_0
  N3: J1.D7, TRRS1.TIP
  N4: J1.GND, C2.0, TRRS1.SLEEVE, Q2.C, R3.Pin_1
  N5: C2.1, TRRS1.RING1, Q2.E
  N6: TRRS1.RING2, C3.1
  N7: Q2.B, R1.Pin_1
  N8: R2.Pin_1, R3.Pin_0, C3.0

notes:
  Black- GND
  Yellow- 3V3_PTT!
  Blue- Audio In
  Orange- Audio Out
  Red- 15V_PTT
