# Fritzing sketch 3_16_20 (saved by Fritzing 0.9.3b)
breadboards: 1

parts:
  J1 = STM32 Nucleo boards
  R1 = Resistor [tolerance=±5% resistance=1k package=THT]
  C1 = Ceramic Capacitor [capacitance=100nF package="100 mil [THT, multilayer]"]
  C2 = Ceramic Capacitor [capacitance=100nF package="100 mil [THT, multilayer]"]
  Q1 = Basic FET P-Channel [package="TO220 [THT]"]
  TRRS1 = Audio Jack (TRRS) 3.5mm [part_number="LUMBERG JEITA RC-5325A" package="RC-5325A [SMD]"]

nets:
  N1: J1.D9_PWM, TRRS1.TIP
  N2: J1.D2, C2.1, Q1.gate
  N3: J1.GND, R1.Pin_1, C1.1, C2.0, TRRS1.SLEEVE
  N4: R1.Pin_0, Q1.drain, TRRS1.RING2
  N5: C1.0, Q1.source, TRRS1.RING1

notes:
  Black- GND
  Yellow- 3V3_PTT!
  Green- 15V_PTT
  Orange- Audio Out
  Red- 15V from Radio
